# Fritzing sketch ir_wiring (saved by Fritzing 0.9.3b)
breadboards: 1

parts:
  R1 = Resistor [tolerance=±5% resistance=100 package="1206 [SMD]"]
  R2 = Resistor [tolerance=±5% resistance=10k package="1206 [SMD]"]
  Infrared_Emitter = LED - 5mm [color="Infrared (940nm)" package="5 mm [THT]"]
  LED2 = LED - 5mm [color="Infrared (850nm)" package="5 mm [THT]"]
  Part1 = Arduino Uno (Rev3)

nets:
  N1: R1.Pin_0, R2.Pin_1, Part1.5V
  N2: R1.Pin_1, Infrared_Emitter.anode
  N3: R2.Pin_0, LED2.cathode, Part1.A0
  N4: Infrared_Emitter.cathode, LED2.anode, Part1.GND

notes:
  Emitter
  Photodiode
